# Fritzing sketch simple_RF_emitter (saved by Fritzing 0.9.2b)
circuit board: 8.46667cm x 5.64444cm

parts:
  Part1 = Arduino Uno (Rev3)
  U1 = RF-LINK_TX [package=rf-link_tx]

nets:
  N1: Part1.D12/MISO, U1.DATA
  GND: Part1.GND, U1.GND
  5V: Part1.5V, U1.+5V
