# Fritzing sketch switch_n_led (saved by Fritzing 0.9.2b)
circuit board: 8.46667cm x 5.64444cm
breadboards: 1

parts:
  Part1 = Arduino Uno (Rev3)
  LED1 = LED - 5mm [color="Red (633nm)" package="5 mm [THT]"]
  R1 = Resistor [tolerance=±5% resistance=220 package=THT]
  S1 = Round Pushbutton

nets:
  N1: Part1.D12/MISO, LED1.anode
  N2: Part1.D3_PWM, S1.leg0
  N3: Part1.GND, R1.Pin_0, S1.leg1
  N4: LED1.cathode, R1.Pin_1
