# Fritzing sketch simple_RF_receiver (saved by Fritzing 0.9.2b)

parts:
  Raspberry_Pi_2_Model_B = Raspberry Pi 2
  U1 = RF-LINK_TX [package=rf-link_tx]

nets:
  GND: Raspberry_Pi_2_Model_B.GND, U1.GND
  N1: Raspberry_Pi_2_Model_B.GPIO27, U1.DATA
  5V: Raspberry_Pi_2_Model_B.5V, U1.+5V
